# Fritzing sketch JS (saved by Fritzing 0.9.6b)

parts:
  S1 = Round Pushbutton
  M1 = gear-motor
  M2 = gear-motor
  Part4 = Arduino Prototyping Shield
  Part6 = Arduino Prototyping Shield
  R2 = Resistor [tolerance=±5% resistance=15k package="0603 [SMD]"]
  R3 = Resistor [tolerance=±5% power=0.25 resistance=15k package=THT]
  R4 = Resistor [tolerance=±5% power=0.25 resistance=15k package=THT]
  R5 = Resistor [tolerance=±5% power=0.25 resistance=15k package=THT]
  R6 = Resistor [tolerance=±5% power=0.25 resistance=15k package=THT]
  kEYPAD_MATRICIAL_1 = KEYPAD 4x3
  Part7 = 12 NeoPixel Ring [part_number=1643]
  JOY1 = Adafruit Arcade Joystick
  Part8 = 0.56" 7-segment LED Backpack [part_number=880]
  S3 = H-Bridge with L298N

nets:
  GND: S1.leg0, Part4.GND, Part6.GND, Part7.GND, JOY1.COM, Part8.GND
  N1: S1.leg1, Part6.D6, Part6.N$178, Part6.N$190, R5.Pin_0
  N2: M1.pin_1, S3.M2-02, S3.ENB-5V
  N3: M1.pin_2, S3.M2-01
  N4: M2.pin_1, S3.M1-02
  N5: M2.pin_2, S3.M1-01
  N6: Part4.D8, S3.IN4
  N7: Part4.D12, Part7.OUT
  N8: Part4.D3, S3.IN1
  N9: Part4.D4, S3.IN2
  N10: Part4.D5, S3.ENA
  N11: Part4.D6, S3.ENB
  N12: Part4.D7, S3.IN3
  N13: Part4.A4, Part6.A4, Part6.N$27, Part6.N$28, Part8.SDA
  N14: Part4.A5, Part6.A5, Part6.N$335, Part6.N$336, Part8.SCL
  +9V: Part4.+9V, Part6.+9V
  N15: Part6.D4, Part6.N$84, Part6.N$90, R3.Pin_0, JOY1.W
  N16: Part6.D5, Part6.N$75, Part6.N$87, R2.Pin_0, JOY1.E
  VDD: Part6.+5V, R2.Pin_1, R3.Pin_1, R4.Pin_1, R5.Pin_1, R6.Pin_1, Part7.VDD, Part8.VDD
  N17: Part6.D8, kEYPAD_MATRICIAL_1.arrow1
  N18: Part6.D9, kEYPAD_MATRICIAL_1.col2
  N19: Part6.D10, kEYPAD_MATRICIAL_1.arrow2
  N20: Part6.D11, kEYPAD_MATRICIAL_1.col3
  N21: Part6.D12, kEYPAD_MATRICIAL_1.arrow4
  N22: Part6.D13, kEYPAD_MATRICIAL_1.arrow3
  N23: Part6.D7, kEYPAD_MATRICIAL_1.col1
  N24: Part6.N$55, R6.Pin_0, JOY1.N
  N25: Part6.N$79, R4.Pin_0, JOY1.S

custom parts:
  KEYPAD 4x3: KEYPAD matricial de 12 botones, 4 filas x 3 columnas
  12 NeoPixel Ring: 12 ultra bright smart LED NeoPixels are arranged in a circle with 1.5" (37mm) outer diameter. The rings are 'chainable' - connect the output pin of one to the input pin of another. Use only one microcontroller pin to control as many as you can chain together! Each LED is addressable as the driver chip is inside the LED. Each one has ~18mA constant current drive so the color will be very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
  0.56" 7-segment LED Backpack: This 0.56" 7-segment LED display includes a driver chip for simple control via an I2C interface. The backpack features address-selection jumpers so you can connect up to eight displays on a single I2C bus.
  H-Bridge with L298N: h-bridge
